# Fritzing sketch ProjectSchem (saved by Fritzing 0.9.3b)
breadboards: 3

parts:
  Part1 = Arduino Uno (Rev3)
  R1 = Resistor [tolerance=±5% resistance=220 package=THT]
  R2 = Resistor [tolerance=±5% resistance=220 package=THT]
  R3 = Resistor [tolerance=±5% resistance=220 package=THT]
  R4 = Resistor [tolerance=±5% resistance=220 package=THT]
  R5 = Resistor [tolerance=±5% resistance=220 package=THT]
  R6 = Resistor [tolerance=±5% resistance=220 package=THT]
  R7 = Resistor [tolerance=±5% resistance=220 package=THT]
  R8 = Resistor [tolerance=±5% resistance=220 package=THT]
  R9 = Resistor [tolerance=±5% resistance=220 package=THT]
  R10 = Resistor [tolerance=±5% resistance=220 package=THT]
  R11 = Resistor [tolerance=±5% resistance=220 package=THT]
  R12 = Resistor [tolerance=±5% resistance=220 package=THT]
  R13 = Resistor [tolerance=±5% resistance=220 package=THT]
  R14 = Resistor [tolerance=±5% resistance=220 package=THT]
  R15 = Resistor [tolerance=±5% resistance=220 package=THT]
  R16 = Resistor [tolerance=±5% resistance=220 package=THT]
  U1 = 74HC595 [package="DIP16 [THT]"]
  U2 = 74HC595 [package="DIP16 [THT]"]
  LED1 = LED - 5mm [color="Blue (430nm)" package="5 mm [THT]"]
  LED2 = LED - 5mm [color="Blue (430nm)" package="5 mm [THT]"]
  LED3 = LED - 5mm [color="Blue (430nm)" package="5 mm [THT]"]
  LED4 = LED - 5mm [color="Blue (430nm)" package="5 mm [THT]"]
  LED5 = LED - 5mm [color="Blue (430nm)" package="5 mm [THT]"]
  LED6 = LED - 5mm [color="White (8000K)" package="5 mm [THT]"]
  LED7 = LED - 5mm [color="White (4500K)" package="5 mm [THT]"]
  LED8 = LED - 5mm [color="Green (565nm)" package="5 mm [THT]"]
  LED9 = LED - 5mm [color="Red (633nm)" package="5 mm [THT]"]
  LED11 = LED - 5mm [color="Red (633nm)" package="5 mm [THT]"]
  LED12 = LED - 5mm [color="Red (633nm)" package="5 mm [THT]"]
  LED13 = LED - 5mm [color="Red (633nm)" package="5 mm [THT]"]
  LED16 = LED - 5mm [color="Red (633nm)" package="5 mm [THT]"]
  LED17 = LED - 5mm [color="Green (565nm)" package="5 mm [THT]"]
  LED18 = LED - 5mm [color="White (4500K)" package="5 mm [THT]"]
  LED19 = LED - 5mm [color="White (8000K)" package="5 mm [THT]"]
  R17 = Resistor [tolerance=±5% resistance=220 package=THT]
  R18 = Resistor [tolerance=±5% resistance=220 package=THT]
  R19 = Resistor [tolerance=±5% resistance=220 package=THT]
  R20 = Resistor [tolerance=±5% resistance=220 package=THT]
  R21 = Resistor [tolerance=±5% resistance=220 package=THT]
  R22 = Resistor [tolerance=±5% resistance=220 package=THT]
  R23 = Resistor [tolerance=±5% resistance=220 package=THT]
  R24 = Resistor [tolerance=±5% resistance=220 package=THT]
  R25 = Resistor [tolerance=±5% resistance=220 package=THT]
  R26 = Resistor [tolerance=±5% resistance=220 package=THT]
  R27 = Resistor [tolerance=±5% resistance=220 package=THT]
  R28 = Resistor [tolerance=±5% resistance=220 package=THT]
  R29 = Resistor [tolerance=±5% resistance=220 package=THT]
  R30 = Resistor [tolerance=±5% resistance=220 package=THT]
  R31 = Resistor [tolerance=±5% resistance=220 package=THT]
  R32 = Resistor [tolerance=±5% resistance=220 package=THT]
  U3 = 74HC595 [package="DIP16 [THT]"]
  U4 = 74HC595 [package="DIP16 [THT]"]
  LED20 = LED - 5mm [color="White (8000K)" package="5 mm [THT]"]
  LED21 = LED - 5mm [color="White (4500K)" package="5 mm [THT]"]
  LED22 = LED - 5mm [color="Green (565nm)" package="5 mm [THT]"]
  LED24 = LED - 5mm [color="Yellow (595nm)" package="5 mm [THT]"]
  LED25 = LED - 5mm [color="Yellow (595nm)" package="5 mm [THT]"]
  LED26 = LED - 5mm [color="Yellow (595nm)" package="5 mm [THT]"]
  LED27 = LED - 5mm [color="Yellow (595nm)" package="5 mm [THT]"]
  LED28 = LED - 5mm [color="Green (565nm)" package="5 mm [THT]"]
  LED29 = LED - 5mm [color="White (4500K)" package="5 mm [THT]"]
  LED30 = LED - 5mm [color="White (8000K)" package="5 mm [THT]"]
  LED31 = LED - 5mm [color="Green (555nm)" package="5 mm [THT]"]
  LED32 = LED - 5mm [color="Green (555nm)" package="5 mm [THT]"]
  LED33 = LED - 5mm [color="Green (555nm)" package="5 mm [THT]"]
  LED34 = LED - 5mm [color="Green (555nm)" package="5 mm [THT]"]
  LED35 = LED - 5mm [color="Green (555nm)" package="5 mm [THT]"]
  LED23 = smd LED [color="Yellow (595nm)" package="0603 [SMD]"]
  Part2 = Arduino Uno (Rev3)
  Part3 = Thumb Joystick
  S1 = Pushbutton [package="[THT]"]
  R33 = Resistor [tolerance=±5% resistance=220 package=THT]
  Serial_LCD = LCD screen

nets:
  N1: Part1.A4/SDA, Part2.A4/SDA, Serial_LCD.RS
  N2: Part1.A5/SCL, Part2.A5/SCL, Serial_LCD.V0
  N3: Part1.D10_PWM/SS, U1.ST_CP, U2.ST_CP, U3.ST_CP, U4.ST_CP
  N4: Part1.D11_PWM/MOSI, U2.DS
  N5: Part1.D12/MISO, U1.SH_CP, U2.SH_CP, U3.SH_CP, U4.SH_CP
  GND: Part1.GND, U1.GND, U1.OE, U2.GND, U2.OE, LED1.cathode, LED2.cathode, LED3.cathode, LED4.cathode, LED5.cathode, LED6.cathode, LED7.cathode, LED8.cathode, LED9.cathode, LED11.cathode, LED12.cathode, LED13.cathode, LED16.cathode, LED17.cathode, LED18.cathode, LED19.cathode, U3.GND, U4.GND, LED20.cathode, LED21.cathode, LED22.cathode, LED24.cathode, LED25.cathode, LED26.cathode, LED27.cathode, LED28.cathode, LED29.cathode, LED30.cathode, LED31.cathode, LED32.cathode, LED33.cathode, LED34.cathode, LED35.cathode, LED23.cathode, Part2.GND, Part3.GND, R33.Pin_0, Serial_LCD.VSS
  N6: R1.Pin_0, LED1.anode
  N7: R1.Pin_1, U1.Q7
  N8: R2.Pin_0, LED2.anode
  N9: R2.Pin_1, U1.Q6
  N10: R3.Pin_0, LED3.anode
  N11: R3.Pin_1, U1.Q5
  N12: R4.Pin_0, LED4.anode
  N13: R4.Pin_1, U1.Q4
  N14: R5.Pin_0, LED5.anode
  N15: R5.Pin_1, U1.Q3
  N16: R6.Pin_0, LED7.anode
  N17: R6.Pin_1, U1.Q1
  N18: R7.Pin_0, LED6.anode
  N19: R7.Pin_1, U1.Q2
  N20: R8.Pin_0, LED11.anode
  N21: R8.Pin_1, U2.Q4
  N22: R9.Pin_0, LED8.anode
  N23: R9.Pin_1, U1.Q0
  N24: R10.Pin_0, LED17.anode
  N25: R10.Pin_1, U2.Q0
  N26: R11.Pin_0, LED18.anode
  N27: R11.Pin_1, U2.Q1
  N28: R12.Pin_0, LED19.anode
  N29: R12.Pin_1, U2.Q2
  N30: R13.Pin_0, LED12.anode
  N31: R13.Pin_1, U2.Q3
  N32: R14.Pin_0, LED16.anode
  N33: R14.Pin_1, U2.Q5
  N34: R15.Pin_0, LED9.anode
  N35: R15.Pin_1, U2.Q6
  N36: R16.Pin_0, LED13.anode
  N37: R16.Pin_1, U2.Q7
  N38: U1.Q7', U3.DS
  VCC: U1.MR, U1.VCC, U2.MR, U2.VCC, U3.MR, U3.VCC, U4.MR, U4.VCC, Part2.5V, Part3.VCC, Serial_LCD.VDD
  N39: U1.DS, U2.Q7'
  N40: R17.Pin_0, LED24.anode
  N41: R17.Pin_1, U3.Q7
  N42: R18.Pin_0, LED27.anode
  N43: R18.Pin_1, U3.Q6
  N44: R19.Pin_0, LED23.anode
  N45: R19.Pin_1, U3.Q5
  N46: R20.Pin_0, LED25.anode
  N47: R20.Pin_1, U3.Q3
  N48: R21.Pin_0, LED20.anode
  N49: R21.Pin_1, U3.Q2
  N50: R22.Pin_0, LED21.anode
  N51: R22.Pin_1, U3.Q1
  N52: R23.Pin_0, LED22.anode
  N53: R23.Pin_1, U3.Q0
  N54: R24.Pin_0, LED28.anode
  N55: R24.Pin_1, U4.Q0
  N56: R25.Pin_0, LED26.anode
  N57: R25.Pin_1, U3.Q4
  N58: R26.Pin_0, LED30.anode
  N59: R26.Pin_1, U4.Q2
  N60: R27.Pin_0, LED29.anode
  N61: R27.Pin_1, U4.Q1
  N62: R28.Pin_0, LED31.anode
  N63: R28.Pin_1, U4.Q3
  N64: R29.Pin_0, LED32.anode
  N65: R29.Pin_1, U4.Q4
  N66: R30.Pin_0, LED33.anode
  N67: R30.Pin_1, U4.Q5
  N68: R31.Pin_0, LED34.anode
  N69: R31.Pin_1, U4.Q6
  N70: R32.Pin_0, LED35.anode
  N71: R32.Pin_1, U4.Q7
  N72: U3.Q7', U4.DS
  N73: U3.OE, U4.OE
  N74: Part2.A0, Part3.HORZ
  N75: Part2.A1, Part3.VERT
  N76: Part2.D1/TX, S1.Pin_3, S1.Pin_4, R33.Pin_1
  N77: S1.Pin_1, S1.Pin_2

notes:
  Serial LCD
  GND VCC SDA SCL
  Pins 4-11 are attached to a keypad.
  Master Arduino
  Slave Arduino
  Master
  Slave
